// Digital circuit 比較.dig as structural Verilog
module \比較  (
  input  x1,
  input  x2,
  input  x3,
  input  y1,
  input  y2,
  input  y3
);

  wire and_6_out, and_7_out, and_9_out, and_10_out, and_11_out, and_12_out, and_13_out, not_1_out, not_2_out,
       not_4_out, not_5_out, not_6_out, not_7_out, not_9_out, not_10_out, not_11_out, not_12_out, not_13_out,
       not_14_out, not_15_out, undriven, undriven_2, undriven_3, undriven_4;

  // And and_1 has open pins: In_1=undriven_4, In_2=not_1_out, out=open
  not not_1 (not_1_out, undriven_3);
  // And and_2 has open pins: In_1=undriven_4, In_2=undriven_3, out=open
  // And and_3 has open pins: In_1=not_2_out, In_2=not_4_out, out=open
  not not_2 (not_2_out, undriven_4);
  not not_3 (not_2_out, undriven_4);
  // Not not_4 has open pins: in=open, out=not_4_out
  // And and_4 has open pins: In_1=not_5_out, In_2=undriven_3, out=open
  not not_5 (not_5_out, undriven_4);
  not not_6 (not_6_out, undriven_2);
  not not_7 (not_7_out, undriven);
  not not_8 (not_7_out, undriven);
  not not_9 (not_9_out, undriven_2);
  not not_10 (not_10_out, undriven);
  // And and_5 has open pins: In_1=undriven, In_2=not_6_out, out=open
  and and_6 (and_6_out, undriven, undriven_2);
  and and_7 (and_7_out, not_7_out, not_9_out);
  // And and_8 has open pins: In_1=not_10_out, In_2=undriven_2, out=open
  // Or or_1 has open pins: In_1=and_6_out, In_2=and_7_out, out=open
  not not_11 (not_11_out, y1);
  not not_12 (not_12_out, x1);
  not not_13 (not_13_out, y2);
  not not_14 (not_14_out, x2);
  not not_15 (not_15_out, x3);
  and and_9 (and_9_out, x1, not_11_out);
  and and_10 (and_10_out, not_12_out, y1);
  and and_11 (and_11_out, x2, not_13_out);
  and and_12 (and_12_out, not_14_out, y2);
  and and_13 (and_13_out, not_15_out, y3);
  // Or or_2 is placed but not wired
endmodule
